// Logisim project calculator.circ as structural Verilog: 9 circuits, main circuit main
module main (
  input  [1:0] in_1,
  input  [1:0] in_2
);

  wire _0_2_out, _0_out, _1_2_out, _1_out, _2_2_out, _2_out, _3_2_out, _3_out, _4_2_out, _4_out, _5_2_out,
       _5_out, _6_2_out, _6_out, _7_2_out, _7_out, _8_2_out, _8_out, _9_2_out, _9_out, button_2_out,
       button_3_out, button_4_out, button_5_out, button_6_out, button_7_out, button_8_out, button_9_out,
       button_10_out, button_out, getopt_1_pressed;
  wire [1:0] getopt_1_opcode;
  wire [3:0] board_1_out_17, board_1_out_18, board_1_out_19, board_1_out_20, board_1_out_21, board_1_out_22,
       board_1_out_23, board_1_out_24, display_1_out_3, display_1_out_4, display_1_out_5, display_1_out_6,
       display_1_out_7, display_1_out_8, display_1_out_9, display_1_out_10;
  wire [31:0] getnum_1_out_11, memory_1_out_6, rom_1_data;

  ROM #(.addrWidth(2), .dataWidth(32)) rom_1 (.addr(in_1), .data(rom_1_data));  // open: sel
  GetNUM getnum_1 (
    ._0(_0_out), ._1(_1_out), ._2(_2_out), ._3(_3_out), ._4(_4_out), ._5(_5_out), ._6(_6_out), ._7(_7_out),
    ._8(_8_out), ._9(_9_out), .out_11(getnum_1_out_11));
  Memory memory_1 (
    .FActor(rom_1_data), .Input(getnum_1_out_11), .OpCode(getopt_1_opcode), .Pressed(getopt_1_pressed),
    .in_2(button_5_out), .out_6(memory_1_out_6));
  Button _7 (.out(_7_out));
  Button _4 (.out(_4_out));
  Button _1 (.out(_1_out));
  Button _8 (.out(_8_out));
  Button _9 (.out(_9_out));
  Button button (.out(button_out));
  Button _6 (.out(_6_out));
  Button _5 (.out(_5_out));
  Button button_2 (.out(button_2_out));
  Button _2 (.out(_2_out));
  Button _3 (.out(_3_out));
  Button button_3 (.out(button_3_out));
  Button _0 (.out(_0_out));
  Button button_4 (.out(button_4_out));
  Button button_5 (.out(button_5_out));
  GetOpt getopt_1 (
    .in_1(button_out), .in_2(button_2_out), .in_3(button_3_out), .in_4(button_4_out), .in_5(button_5_out),
    .OpCode(getopt_1_opcode), .Pressed(getopt_1_pressed));
  Hex_Digit_Display hex_digit_display_1 (.value(board_1_out_17));  // open: dp
  Hex_Digit_Display hex_digit_display_2 (.value(display_1_out_3));  // open: dp
  Hex_Digit_Display hex_digit_display_3 (.value(display_1_out_10));  // open: dp
  Hex_Digit_Display hex_digit_display_4 (.value(board_1_out_19));  // open: dp
  Hex_Digit_Display hex_digit_display_5 (.value(board_1_out_18));  // open: dp
  Button _7_2 (.out(_7_2_out));
  Button _4_2 (.out(_4_2_out));
  Button _1_2 (.out(_1_2_out));
  Hex_Digit_Display hex_digit_display_6 (.value(display_1_out_4));  // open: dp
  Hex_Digit_Display hex_digit_display_7 (.value(display_1_out_5));  // open: dp
  Display display_1 (
    .Factor(rom_1_data), .out_10(display_1_out_10), .out_3(display_1_out_3), .out_4(display_1_out_4),
    .out_5(display_1_out_5), .out_6(display_1_out_6), .out_7(display_1_out_7), .out_8(display_1_out_8),
    .out_9(display_1_out_9), .NUM(memory_1_out_6));
  Hex_Digit_Display hex_digit_display_8 (.value(board_1_out_20));  // open: dp
  Hex_Digit_Display hex_digit_display_9 (.value(board_1_out_21));  // open: dp
  Board board_1 (
    .in_1(in_2), .out_17(board_1_out_17), .out_18(board_1_out_18), .out_19(board_1_out_19),
    .out_20(board_1_out_20), .out_21(board_1_out_21), .out_22(board_1_out_22), .out_23(board_1_out_23),
    .out_24(board_1_out_24), ._0(_0_2_out), ._1(_1_2_out), ._2(_2_2_out), ._3(_3_2_out), ._4(_4_2_out),
    ._5(_5_2_out), ._6(_6_2_out), ._7(_7_2_out), ._8(_8_2_out), ._9(_9_2_out), .in_14(button_7_out),
    .in_7(button_8_out), .in_15(button_9_out), .in_8(button_10_out), .in_16(button_6_out));
  Button _8_2 (.out(_8_2_out));
  Button _9_2 (.out(_9_2_out));
  Button _6_2 (.out(_6_2_out));
  Button _5_2 (.out(_5_2_out));
  Button _2_2 (.out(_2_2_out));
  Button _3_2 (.out(_3_2_out));
  Button _0_2 (.out(_0_2_out));
  Button button_6 (.out(button_6_out));
  Hex_Digit_Display hex_digit_display_10 (.value(display_1_out_6));  // open: dp
  Hex_Digit_Display hex_digit_display_11 (.value(display_1_out_7));  // open: dp
  Hex_Digit_Display hex_digit_display_12 (.value(board_1_out_22));  // open: dp
  Hex_Digit_Display hex_digit_display_13 (.value(board_1_out_23));  // open: dp
  Button button_7 (.out(button_7_out));
  Button button_8 (.out(button_8_out));
  Button button_9 (.out(button_9_out));
  Button button_10 (.out(button_10_out));
  Hex_Digit_Display hex_digit_display_14 (.value(display_1_out_9));  // open: dp
  Hex_Digit_Display hex_digit_display_15 (.value(display_1_out_8));  // open: dp
  Hex_Digit_Display hex_digit_display_16 (.value(board_1_out_24));  // open: dp

  // Notes on the sheet:
  //   contents of rom_1 (hex, n*v repeats v):
  //   a
endmodule

module GetNUM (
  input  _0,
  input  _1,
  input  _2,
  input  _3,
  input  _4,
  input  _5,
  input  _6,
  input  _7,
  input  _8,
  input  _9,
  output [31:0] out_11
);

  wire and_1_out, and_2_out, and_3_out, and_4_out, and_5_out, and_6_out, and_7_out, and_8_out, and_9_out,
       and_10_out, xor_1_out;
  wire [1:0] bit_extender_1_out, bit_extender_2_out, bit_extender_3_out, bit_extender_4_out,
       bit_extender_5_out, bit_extender_6_out, bit_extender_7_out, bit_extender_8_out, bit_extender_9_out,
       bit_extender_10_out;

  ExactlyOne xor_1 (
    .out(xor_1_out), .in0(_0), .in1(_1), .in2(_2), .in3(_3), .in4(_4), .in5(_5), .in6(_6), .in7(_7),
    .in8(_8), .in9(_9));
  and and_1 (and_1_out, _0, xor_1_out);
  and and_2 (and_2_out, _1, xor_1_out);
  and and_3 (and_3_out, _2, xor_1_out);
  and and_4 (and_4_out, _3, xor_1_out);
  and and_5 (and_5_out, _4, xor_1_out);
  and and_6 (and_6_out, _5, xor_1_out);
  and and_7 (and_7_out, _6, xor_1_out);
  and and_8 (and_8_out, _7, xor_1_out);
  and and_9 (and_9_out, _8, xor_1_out);
  and and_10 (and_10_out, _9, xor_1_out);
  assign bit_extender_1_out = {{1{1'b0}}, and_1_out};  // Bit_Extender bit_extender_1
  assign bit_extender_2_out = {{1{1'b0}}, and_2_out};  // Bit_Extender bit_extender_2
  assign bit_extender_3_out = {{1{1'b0}}, and_3_out};  // Bit_Extender bit_extender_3
  assign bit_extender_4_out = {{1{1'b0}}, and_4_out};  // Bit_Extender bit_extender_4
  assign bit_extender_5_out = {{1{1'b0}}, and_5_out};  // Bit_Extender bit_extender_5
  assign bit_extender_6_out = {{1{1'b0}}, and_6_out};  // Bit_Extender bit_extender_6
  assign bit_extender_7_out = {{1{1'b0}}, and_7_out};  // Bit_Extender bit_extender_7
  assign bit_extender_8_out = {{1{1'b0}}, and_8_out};  // Bit_Extender bit_extender_8
  assign bit_extender_9_out = {{1{1'b0}}, and_9_out};  // Bit_Extender bit_extender_9
  assign bit_extender_10_out = {{1{1'b0}}, and_10_out};  // Bit_Extender bit_extender_10
  ROM #(.addrWidth(2), .dataWidth(32)) rom_1 (.addr(bit_extender_1_out), .data(out_11), .sel(and_1_out));
  ROM #(.addrWidth(2), .dataWidth(32)) rom_2 (.addr(bit_extender_2_out), .data(out_11), .sel(and_2_out));
  ROM #(.addrWidth(2), .dataWidth(32)) rom_3 (.addr(bit_extender_3_out), .data(out_11), .sel(and_3_out));
  ROM #(.addrWidth(2), .dataWidth(32)) rom_4 (.addr(bit_extender_4_out), .data(out_11), .sel(and_4_out));
  ROM #(.addrWidth(2), .dataWidth(32)) rom_5 (.addr(bit_extender_5_out), .data(out_11), .sel(and_5_out));
  ROM #(.addrWidth(2), .dataWidth(32)) rom_6 (.addr(bit_extender_6_out), .data(out_11), .sel(and_6_out));
  ROM #(.addrWidth(2), .dataWidth(32)) rom_7 (.addr(bit_extender_7_out), .data(out_11), .sel(and_7_out));
  ROM #(.addrWidth(2), .dataWidth(32)) rom_8 (.addr(bit_extender_8_out), .data(out_11), .sel(and_8_out));
  ROM #(.addrWidth(2), .dataWidth(32)) rom_9 (.addr(bit_extender_9_out), .data(out_11), .sel(and_9_out));
  ROM #(.addrWidth(2), .dataWidth(32)) rom_10 (.addr(bit_extender_10_out), .data(out_11), .sel(and_10_out));

  // Notes on the sheet:
  //   contents of rom_2 (hex, n*v repeats v):
  //   0 1
  //   contents of rom_3 (hex, n*v repeats v):
  //   0 2
  //   contents of rom_4 (hex, n*v repeats v):
  //   0 3
  //   contents of rom_5 (hex, n*v repeats v):
  //   0 4
  //   contents of rom_6 (hex, n*v repeats v):
  //   0 5
  //   contents of rom_7 (hex, n*v repeats v):
  //   0 6
  //   contents of rom_8 (hex, n*v repeats v):
  //   0 7
  //   contents of rom_9 (hex, n*v repeats v):
  //   0 8
  //   contents of rom_10 (hex, n*v repeats v):
  //   0 9
endmodule

module Memory (
  input  [31:0] FActor,
  input  in_2,
  input  [31:0] Input,
  input  [1:0] OpCode,
  input  Pressed,
  output [31:0] out_6
);

  wire andc1_1_out_3, B_2_q, clock_1_out, not_1_out, not_2_out, not_3_out, not_4_out;
  wire [1:0] A_q, B_q;
  wire [31:0] A_3_q, A_4_q, A_5_q, A_6_q, adder_1_out, alu_1_out, Buffer_out, multiplier_1_out;

  Register #(.width(2)) A (.D(B_q), .en(clock_1_out), .Q(A_q), .clk(clock_1_out));  // open: clr
  Register #(.width(2)) B (.D(OpCode), .en(not_1_out), .Q(B_q), .clk(clock_1_out));  // open: clr
  not not_1 (not_1_out, clock_1_out);
  not not_2 (not_2_out, clock_1_out);
  Clock clock_1 (.out(clock_1_out));
  Register #(.width(1)) A_2 (.D(B_2_q), .en(clock_1_out), .clk(clock_1_out));  // open: Q, clr
  Register #(.width(1)) B_2 (.D(Pressed), .en(not_2_out), .Q(B_2_q), .clk(clock_1_out));  // open: clr
  Multiplier #(.width(32)) multiplier_1 (.a(A_3_q), .b(FActor), .out(multiplier_1_out));  // open: cin, cout
  Adder #(.width(32)) adder_1 (.a(multiplier_1_out), .b(Input), .out(adder_1_out));  // open: cin, cout
  Register #(.width(32)) A_3 (.D(A_4_q), .en(clock_1_out), .Q(A_3_q), .clk(clock_1_out));  // open: clr
  Register #(.width(32)) A_4 (.D(adder_1_out), .en(not_3_out), .Q(A_4_q), .clk(clock_1_out), .clr(B_2_q));
  not not_3 (not_3_out, clock_1_out);
  AndC1 andc1_1 (.word(A_4_q), .Press(Pressed), .out_3(andc1_1_out_3));
  Hex_Digit_Display hex_digit_display_1 (.value(A_4_q[27:24]));  // open: dp
  Hex_Digit_Display hex_digit_display_2 (.value(A_4_q[31:28]));  // open: dp
  assign Buffer_out = andc1_1_out_3 ? A_4_q : 32'bz;  // Controlled_Buffer Buffer
  Hex_Digit_Display hex_digit_display_3 (.value(A_4_q[19:16]));  // open: dp
  Hex_Digit_Display hex_digit_display_4 (.value(A_4_q[23:20]));  // open: dp
  ALU alu_1 (.A(A_5_q), .B(Buffer_out), .OpCode(A_q), .Out(alu_1_out));
  not not_4 (not_4_out, clock_1_out);
  Hex_Digit_Display hex_digit_display_5 (.value(A_4_q[11:8]));  // open: dp
  Hex_Digit_Display hex_digit_display_6 (.value(A_4_q[15:12]));  // open: dp
  Register #(.width(32)) A_5 (.D(A_6_q), .en(clock_1_out), .Q(A_5_q), .clk(clock_1_out));  // open: clr
  Register #(.width(32)) A_6 (.D(alu_1_out), .en(not_4_out), .Q(A_6_q), .clk(clock_1_out));  // open: clr
  Hex_Digit_Display hex_digit_display_7 (.value(A_4_q[3:0]));  // open: dp
  Hex_Digit_Display hex_digit_display_8 (.value(A_4_q[7:4]));  // open: dp
  Multiplexer #(.width(32)) multiplexer_1 (.in0(A_4_q), .in1(A_6_q), .out(out_6), .sel(in_2));  // open: en
endmodule

module ALU (
  input  [31:0] A,
  input  [31:0] B,
  input  [1:0] OpCode,
  output [31:0] Out
);

  wire [31:0] adder_1_out, divider_1_out, multiplier_1_out, subtractor_1_out;

  Adder #(.width(32)) adder_1 (.a(A), .b(B), .out(adder_1_out));  // open: cin, cout
  Subtractor #(.width(32)) subtractor_1 (.a(A), .b(B), .out(subtractor_1_out));  // open: bin, bout
  Multiplier #(.width(32)) multiplier_1 (.a(A), .b(B), .out(multiplier_1_out));  // open: cin, cout
  Divider #(.width(32)) divider_1 (.a(A), .b(B), .out(divider_1_out));  // open: upper, rem
  Multiplexer #(.select(2), .width(32)) multiplexer_1 (
    .in0(adder_1_out), .in1(subtractor_1_out), .in2(multiplier_1_out), .in3(divider_1_out), .out(Out),
    .sel(OpCode));  // open: en
endmodule

module GetOpt (
  input  in_1,
  input  in_2,
  input  in_3,
  input  in_4,
  input  in_5,
  output [1:0] OpCode,
  output Pressed
);

  wire and_1_out, and_2_out, and_3_out, and_4_out, and_5_out;
  wire [1:0] bit_extender_1_out, bit_extender_2_out, bit_extender_3_out, bit_extender_4_out,
       bit_extender_5_out;

  ExactlyOne xor_1 (.out(Pressed), .in0(in_1), .in1(in_2), .in2(in_5), .in3(in_3), .in4(in_4));
  and and_1 (and_1_out, in_1, Pressed);
  and and_2 (and_2_out, in_2, Pressed);
  and and_3 (and_3_out, in_3, Pressed);
  and and_4 (and_4_out, in_4, Pressed);
  and and_5 (and_5_out, in_5, Pressed);
  assign bit_extender_1_out = {{1{1'b0}}, and_1_out};  // Bit_Extender bit_extender_1
  assign bit_extender_2_out = {{1{1'b0}}, and_2_out};  // Bit_Extender bit_extender_2
  assign bit_extender_3_out = {{1{1'b0}}, and_3_out};  // Bit_Extender bit_extender_3
  assign bit_extender_4_out = {{1{1'b0}}, and_4_out};  // Bit_Extender bit_extender_4
  assign bit_extender_5_out = {{1{1'b0}}, and_5_out};  // Bit_Extender bit_extender_5
  ROM #(.addrWidth(2), .dataWidth(2)) rom_1 (.addr(bit_extender_1_out), .data(OpCode), .sel(and_1_out));
  ROM #(.addrWidth(2), .dataWidth(2)) rom_2 (.addr(bit_extender_2_out), .data(OpCode), .sel(and_2_out));
  ROM #(.addrWidth(2), .dataWidth(2)) rom_3 (.addr(bit_extender_3_out), .data(OpCode), .sel(and_3_out));
  ROM #(.addrWidth(2), .dataWidth(2)) rom_4 (.addr(bit_extender_4_out), .data(OpCode), .sel(and_4_out));
  ROM #(.addrWidth(2), .dataWidth(2)) rom_5 (.addr(bit_extender_5_out), .data(OpCode), .sel(and_5_out));

  // Notes on the sheet:
  //   contents of rom_2 (hex, n*v repeats v):
  //   0 1
  //   contents of rom_3 (hex, n*v repeats v):
  //   0 2
  //   contents of rom_4 (hex, n*v repeats v):
  //   0 3
endmodule

module AndC1 (
  input  [31:0] word,
  input  Press,
  output out_3
);

  wire or_1_out;

  or or_1 (or_1_out, word[0], word[1], word[2], word[3], word[4], word[5], word[6], word[7], word[8], word[9], word[10], word[11], word[12], word[13], word[14], word[15], word[16], word[17], word[18], word[19], word[20], word[21], word[22], word[23], word[24], word[25], word[26], word[27], word[28], word[29], word[30], word[31]);
  and and_1 (out_3, or_1_out, Press);
endmodule

module Mod (
  input  [31:0] A,
  input  [31:0] B,
  output [31:0] out_3
);

  Divider #(.width(32)) divider_1 (.a(A), .b(B), .rem(out_3));  // open: out, upper
endmodule

module Display (
  input  [31:0] NUM,
  input  [31:0] Factor,
  output [3:0] out_3,
  output [3:0] out_4,
  output [3:0] out_5,
  output [3:0] out_6,
  output [3:0] out_7,
  output [3:0] out_8,
  output [3:0] out_9,
  output [3:0] out_10
);

  wire [3:0] divider_3_out_2, divider_3_out_3, divider_3_out_4, divider_3_out_5, divider_6_out,
       divider_6_out_2, divider_6_out_3, divider_6_out_4, divider_6_out_5;
  wire [15:4] divider_3_out;
  wire [31:0] mod_1_out_3, mod_2_out_3, mod_3_out_3, mod_4_out_3, mod_5_out_3, mod_6_out_3, mod_7_out_3,
       multiplier_1_out, multiplier_2_out, multiplier_3_out, multiplier_4_out, multiplier_5_out,
       multiplier_6_out, multiplier_7_out, subtractor_1_out, subtractor_2_out, subtractor_3_out,
       subtractor_4_out, subtractor_5_out, subtractor_6_out, subtractor_7_out;
  wire [31:4] divider_1_out, divider_2_out, divider_4_out, divider_5_out, divider_7_out, mod_8_out_3;
  wire [31:24] divider_6_out_6;

  Mod mod_1 (.out_3(mod_1_out_3), .A(NUM), .B(multiplier_1_out));
  Multiplier #(.width(32)) multiplier_1 (.a(multiplier_2_out), .b(Factor), .out(multiplier_1_out));  // open: cin, cout
  Subtractor #(.width(32)) subtractor_1 (.a(mod_1_out_3), .b(mod_2_out_3), .out(subtractor_1_out));  // open: bin, bout
  Multiplier #(.width(32)) multiplier_2 (.a(multiplier_3_out), .b(Factor), .out(multiplier_2_out));  // open: cin, cout
  Divider #(.width(32)) divider_1 (
    .a(subtractor_1_out), .b(multiplier_2_out), .out({divider_1_out, out_10}));  // open: upper, rem
  Mod mod_2 (.out_3(mod_2_out_3), .A(NUM), .B(multiplier_2_out));
  Subtractor #(.width(32)) subtractor_2 (.a(mod_2_out_3), .b(mod_3_out_3), .out(subtractor_2_out));  // open: bin, bout
  Mod mod_3 (.out_3(mod_3_out_3), .A(NUM), .B(multiplier_3_out));
  Multiplier #(.width(32)) multiplier_3 (.a(multiplier_4_out), .b(Factor), .out(multiplier_3_out));  // open: cin, cout
  Divider #(.width(32)) divider_2 (
    .a(subtractor_2_out), .b(multiplier_3_out), .out({divider_2_out, out_3}));  // open: upper, rem
  Subtractor #(.width(32)) subtractor_3 (.a(mod_3_out_3), .b(mod_4_out_3), .out(subtractor_3_out));  // open: bin, bout
  Multiplier #(.width(32)) multiplier_4 (.a(multiplier_5_out), .b(Factor), .out(multiplier_4_out));  // open: cin, cout
  Divider #(.width(32)) divider_3 (
    .a(subtractor_3_out), .b(multiplier_4_out),
    .out({divider_3_out_5, divider_3_out_4, divider_3_out_3, divider_3_out_2, divider_3_out, out_4}));  // open: upper, rem
  Mod mod_4 (.out_3(mod_4_out_3), .A(NUM), .B(multiplier_4_out));
  Subtractor #(.width(32)) subtractor_4 (.a(mod_4_out_3), .b(mod_5_out_3), .out(subtractor_4_out));  // open: bin, bout
  Multiplier #(.width(32)) multiplier_5 (.a(multiplier_6_out), .b(Factor), .out(multiplier_5_out));  // open: cin, cout
  Divider #(.width(32)) divider_4 (
    .a(subtractor_4_out), .b(multiplier_5_out), .out({divider_4_out, out_5}));  // open: upper, rem
  Mod mod_5 (.out_3(mod_5_out_3), .A(NUM), .B(multiplier_5_out));
  Subtractor #(.width(32)) subtractor_5 (.a(mod_5_out_3), .b(mod_6_out_3), .out(subtractor_5_out));  // open: bin, bout
  Mod mod_6 (.out_3(mod_6_out_3), .A(NUM), .B(multiplier_6_out));
  Multiplier #(.width(32)) multiplier_6 (.a(multiplier_7_out), .b(Factor), .out(multiplier_6_out));  // open: cin, cout
  Divider #(.width(32)) divider_5 (
    .a(subtractor_5_out), .b(multiplier_6_out), .out({divider_5_out, out_6}));  // open: upper, rem
  Subtractor #(.width(32)) subtractor_6 (.a(mod_6_out_3), .b(mod_7_out_3), .out(subtractor_6_out));  // open: bin, bout
  Divider #(.width(32)) divider_6 (
    .a(subtractor_6_out), .b(multiplier_7_out),
    .out({divider_6_out_6, divider_6_out_5, divider_6_out_4, divider_6_out_3, divider_6_out_2, divider_6_out, out_7}));  // open: upper, rem
  Mod mod_7 (.out_3(mod_7_out_3), .A(NUM), .B(multiplier_7_out));
  Multiplier #(.width(32)) multiplier_7 (.a(Factor), .b(Factor), .out(multiplier_7_out));  // open: cin, cout
  Subtractor #(.width(32)) subtractor_7 (
    .a(mod_7_out_3), .b({mod_8_out_3, out_9}), .out(subtractor_7_out));  // open: bin, bout
  Divider #(.width(32)) divider_7 (.a(subtractor_7_out), .b(Factor), .out({divider_7_out, out_8}));  // open: upper, rem
  Mod mod_8 (.out_3({mod_8_out_3, out_9}), .A(NUM), .B(Factor));
endmodule

module Board (
  input  [1:0] in_1,
  input  _0,
  input  _2,
  input  _4,
  input  _6,
  input  _8,
  input  in_7,
  input  in_8,
  input  _1,
  input  _3,
  input  _5,
  input  _7,
  input  _9,
  input  in_14,
  input  in_15,
  input  in_16,
  output [3:0] out_17,
  output [3:0] out_18,
  output [3:0] out_19,
  output [3:0] out_20,
  output [3:0] out_21,
  output [3:0] out_22,
  output [3:0] out_23,
  output [3:0] out_24
);

  wire getopt_1_pressed;
  wire [1:0] getopt_1_opcode;
  wire [31:0] getnum_1_out_11, memory_1_out_6, rom_1_data;

  ROM #(.addrWidth(2), .dataWidth(32)) rom_1 (.addr(in_1), .data(rom_1_data));  // open: sel
  GetNUM getnum_1 (
    ._0(_0), ._1(_1), ._2(_2), ._3(_3), ._4(_4), ._5(_5), ._6(_6), ._7(_7), ._8(_8), ._9(_9),
    .out_11(getnum_1_out_11));
  Memory memory_1 (
    .FActor(rom_1_data), .Input(getnum_1_out_11), .OpCode(getopt_1_opcode), .Pressed(getopt_1_pressed),
    .in_2(in_16), .out_6(memory_1_out_6));
  GetOpt getopt_1 (
    .in_1(in_14), .in_2(in_7), .in_3(in_15), .in_4(in_8), .in_5(in_16), .OpCode(getopt_1_opcode),
    .Pressed(getopt_1_pressed));
  Display display_1 (
    .Factor(rom_1_data), .out_10(out_17), .out_3(out_18), .out_4(out_19), .out_5(out_20), .out_6(out_21),
    .out_7(out_22), .out_8(out_23), .out_9(out_24), .NUM(memory_1_out_6));

  // Notes on the sheet:
  //   contents of rom_1 (hex, n*v repeats v):
  //   a
endmodule
